// Logisim project project.circ as structural Verilog
module main (
);

  wire clk, clk_screen, comparator_1_eq, comparator_2_eq, comparator_3_eq, comparator_4_eq, comparator_5_eq,
       keyboard_1_avail, R, Reset, rgb_video_1_p2;
  wire [3:0] X, Y;
  wire [6:0] keyboard_1_data;
  wire [23:0] color;
  wire [31:0] bit_extender_1_out, cpu_1_adress, data, register_1_q;
  wire [31:1] clk_screen_q, R_q;
  wire [31:4] X_q, Y_q;
  wire [31:24] color_q;

  Clock clock_1 (.out(clk));
  Button button_1 (.out(R));
  cpu cpu_1 (.data_in(register_1_q), .reset(R), .clk(clk), .value(data), .adress(cpu_1_adress));
  // Probe on data
  Comparator #(.width(32)) comparator_1 (.a(cpu_1_adress), .b(32'h200), .eq(comparator_1_eq));  // open: gt, lt
  Comparator #(.width(32)) comparator_2 (.a(cpu_1_adress), .b(32'h204), .eq(comparator_2_eq));  // open: gt, lt
  Comparator #(.width(32)) comparator_3 (.a(cpu_1_adress), .b(32'h208), .eq(comparator_3_eq));  // open: gt, lt
  Comparator #(.width(32)) comparator_4 (.a(cpu_1_adress), .b(32'h20c), .eq(comparator_4_eq));  // open: gt, lt
  Comparator #(.width(32)) comparator_5 (.a(cpu_1_adress), .b(32'h210), .eq(comparator_5_eq));  // open: gt, lt
  Register #(.width(32)) u_color (.D(data), .en(comparator_1_eq), .Q({color_q, color}), .clk(clk), .clr(R));
  Register #(.width(32)) u_X (.D(data), .en(comparator_2_eq), .Q({X_q, X}), .clk(clk), .clr(R));
  Register #(.width(32)) u_Y (.D(data), .en(comparator_3_eq), .Q({Y_q, Y}), .clk(clk), .clr(R));
  Register #(.width(32)) u_R (.D(data), .en(comparator_4_eq), .Q({R_q, Reset}), .clk(clk), .clr(R));
  Register #(.width(32)) u_clk_screen (
    .D(data), .en(comparator_5_eq), .Q({clk_screen_q, clk_screen}), .clk(clk), .clr(R));
  // RGB_Video #(.cursor("No Cursor"), .height(16), .reset("Synchronous"), .scale(8), .width(16)) rgb_video_1: pin names not known; wires that end beside it: Reset, rgb_video_1_p2, 1'b1, X, Y, color
  or or_1 (rgb_video_1_p2, Reset, clk_screen);
  Keyboard #(.buflen(1)) keyboard_1 (
    .clk(clk), .re(1'b1), .avail(keyboard_1_avail), .data(keyboard_1_data));  // open: clr
  // Probe on X
  // Probe on Y
  assign bit_extender_1_out = {{25{1'b0}}, keyboard_1_data};  // Bit_Extender bit_extender_1
  Register #(.width(32)) register_1 (
    .D(bit_extender_1_out), .clk(keyboard_1_avail), .Q(register_1_q));  // open: en, clr
  // Probe on register_1_q
endmodule

module PC (
  input  [31:0] imm_b,
  input  [31:0] imm_j,
  input  [31:0] rs1_val,
  input  clk,
  input  [31:0] imm_i,
  input  reset,
  input  branch_taken,
  input  jump,
  input  jalr,
  output [31:0] pc_out,
  output [31:0] pc_plus_4
);

  wire [31:0] adder_1_out, adder_3_out, adder_4_out, and_1_out, multiplexer_1_out, multiplexer_2_out,
       multiplexer_3_out;

  Register #(.width(32)) pc_reg (.D(multiplexer_3_out), .en(1'b1), .clk(clk), .Q(pc_out), .clr(reset));
  Adder #(.width(32)) adder_1 (.a(rs1_val), .b(imm_i), .out(adder_1_out));  // open: cin, cout
  Adder #(.width(32)) adder_2 (.a(pc_out), .b(32'h4), .out(pc_plus_4));  // open: cin, cout
  Adder #(.width(32)) adder_3 (.a(pc_out), .b(imm_b), .out(adder_3_out));  // open: cin, cout
  Adder #(.width(32)) adder_4 (.a(pc_out), .b(imm_j), .out(adder_4_out));  // open: cin, cout
  assign and_1_out = adder_1_out & 32'hfffffffe;  // AND_Gate and_1, 32 bits wide
  Multiplexer #(.width(32)) multiplexer_1 (
    .in0(pc_plus_4), .in1(adder_3_out), .out(multiplexer_1_out), .sel(branch_taken));
  Multiplexer #(.width(32)) multiplexer_2 (
    .in0(multiplexer_1_out), .in1(adder_4_out), .out(multiplexer_2_out), .sel(jump));
  Multiplexer #(.width(32)) multiplexer_3 (
    .in0(multiplexer_2_out), .in1(and_1_out), .out(multiplexer_3_out), .sel(jalr));

  // Notes on the sheet:
  //   pc_next
endmodule

module InstMem (
  input  [7:0] in_1,
  output [31:0] out_2
);

  ROM #(.dataWidth(32)) rom_1 (.addr(in_1), .data(out_2));

  // Notes on the sheet:
  //   contents of rom_1 (hex, n*v repeats v):
  //   500093 a00113 2081b3 302023 2203
endmodule

module ImmGen (
  input  [31:0] instr,
  input  [2:0] imm_sel,
  output [31:0] type_i,
  output [31:0] imm_out,
  output [31:0] type_b,
  output [31:0] type_j
);

  wire [31:0] bit_extender_1_out;

  assign bit_extender_1_out = {{20{instr[31]}}, {instr[31:25], instr[11:7]}};  // Bit_Extender bit_extender_1
  assign type_i = {{20{instr[31]}}, instr[31:20]};  // Bit_Extender bit_extender_2
  assign type_b = {{19{instr[31]}}, {instr[31], instr[7], instr[30:25], instr[11:8], 1'b0}};  // Bit_Extender bit_extender_3
  assign type_j = {{11{instr[31]}}, {instr[31], instr[19:12], instr[20], instr[30:21], 1'b0}};  // Bit_Extender bit_extender_4
  Multiplexer #(.select(3), .width(32)) multiplexer_1 (
    .in0(type_i), .in1(bit_extender_1_out), .in2(type_b), .in3({instr[31:12], {12{1'b0}}}), .in4(type_j),
    .out(imm_out), .sel(imm_sel));  // open: in5, in6, in7

  // Other names for the same wires on the sheet: p11_8[3:0] = instr[11:8]; p7 = instr[7]; p30_21[9:0] = instr[30:21];
  //   p31_12[19:0] = instr[31:12]; p30_25[5:0] = instr[30:25]; p20 = instr[20]; p19_12[7:0] = instr[19:12];
  //   p31 = instr[31]; p0 = instr[0]

  // Notes on the sheet:
  //   type-s
  //   type-i
  //   type-B
  //   type-u
  //   type-j
endmodule

module RegFile (
  input  [31:0] alu_result,
  input  [31:0] ram_read_data,
  input  [31:0] Pc_plus_4,
  input  [1:0] MemtoReg,
  input  clk,
  input  RegWrite,
  input  Reset,
  input  [4:0] rd_index,
  input  [4:0] rs1_index,
  input  [4:0] rs2_index,
  output [31:0] rs1_data,
  output [31:0] rs2_data
);

  wire demultiplexer_1_out0, demultiplexer_1_out1, demultiplexer_1_out2, demultiplexer_1_out3;
  wire [7:0] demultiplexer_2_out0, demultiplexer_3_out0, demultiplexer_4_out0, demultiplexer_5_out0;
  wire [31:0] write_data, x1_ra_q, x2_sp_q, x3_gp_q, x4_tp_q, x5_t0_q, x6_t1_q, x7_t2_q, x8_s0_q, x9_s1_q,
       x10_a0_q, x11_a1_q, x12_a2_q, x13_a3_q, x14_a4_q, x15_a5_q, x16_a6_q, x17_a7_q, x18_s2_q, x19_s3_q,
       x20_s4_q, x21_s5_q, x22_s6_q, x23_s7_q, x24_s8_q, x25_s9_q, x26_s10_q, x27_s11_q, x28_t3_q, x29_t4_q,
       x30_t5_q, x31_t6_q;

  Demultiplexer #(.select(2)) demultiplexer_1 (
    .out0(demultiplexer_1_out0), .out1(demultiplexer_1_out1), .out2(demultiplexer_1_out2),
    .out3(demultiplexer_1_out3), .in(RegWrite), .sel(rd_index[4:3]));
  Multiplexer #(.select(2), .width(32)) multiplexer_1 (
    .in0(alu_result), .in1(ram_read_data), .in2(Pc_plus_4), .in3({32{1'b0}}), .out(write_data), .sel(MemtoReg));
  // Probe on write_data
  Demultiplexer #(.select(3)) demultiplexer_2 (
    .out0(demultiplexer_2_out0[0]), .out1(demultiplexer_2_out0[1]), .out2(demultiplexer_2_out0[2]),
    .out3(demultiplexer_2_out0[3]), .out4(demultiplexer_2_out0[4]), .out5(demultiplexer_2_out0[5]),
    .out6(demultiplexer_2_out0[6]), .out7(demultiplexer_2_out0[7]), .in(demultiplexer_1_out0),
    .sel(rd_index[2:0]));
  Demultiplexer #(.select(3)) demultiplexer_3 (
    .out0(demultiplexer_3_out0[0]), .out1(demultiplexer_3_out0[1]), .out2(demultiplexer_3_out0[2]),
    .out3(demultiplexer_3_out0[3]), .out4(demultiplexer_3_out0[4]), .out5(demultiplexer_3_out0[5]),
    .out6(demultiplexer_3_out0[6]), .out7(demultiplexer_3_out0[7]), .in(demultiplexer_1_out1),
    .sel(rd_index[2:0]));
  Demultiplexer #(.select(3)) demultiplexer_4 (
    .out0(demultiplexer_4_out0[0]), .out1(demultiplexer_4_out0[1]), .out2(demultiplexer_4_out0[2]),
    .out3(demultiplexer_4_out0[3]), .out4(demultiplexer_4_out0[4]), .out5(demultiplexer_4_out0[5]),
    .out6(demultiplexer_4_out0[6]), .out7(demultiplexer_4_out0[7]), .in(demultiplexer_1_out2),
    .sel(rd_index[2:0]));
  Demultiplexer #(.select(3)) demultiplexer_5 (
    .out0(demultiplexer_5_out0[0]), .out1(demultiplexer_5_out0[1]), .out2(demultiplexer_5_out0[2]),
    .out3(demultiplexer_5_out0[3]), .out4(demultiplexer_5_out0[4]), .out5(demultiplexer_5_out0[5]),
    .out6(demultiplexer_5_out0[6]), .out7(demultiplexer_5_out0[7]), .in(demultiplexer_1_out3),
    .sel(rd_index[2:0]));
  Register #(.width(32)) x8_s0 (.D(write_data), .en(demultiplexer_3_out0[0]), .clk(clk), .Q(x8_s0_q), .clr(Reset));
  Register #(.width(32)) x16_a6 (.D(write_data), .en(demultiplexer_4_out0[0]), .clk(clk), .Q(x16_a6_q), .clr(Reset));
  Register #(.width(32)) x24_s8 (.D(write_data), .en(demultiplexer_5_out0[0]), .clk(clk), .Q(x24_s8_q), .clr(Reset));
  Register #(.width(32)) x1_ra (.D(write_data), .en(demultiplexer_2_out0[1]), .clk(clk), .Q(x1_ra_q), .clr(Reset));
  Register #(.width(32)) x9_s1 (.D(write_data), .en(demultiplexer_3_out0[1]), .clk(clk), .Q(x9_s1_q), .clr(Reset));
  Register #(.width(32)) x17_a7 (.D(write_data), .en(demultiplexer_4_out0[1]), .clk(clk), .Q(x17_a7_q), .clr(Reset));
  Register #(.width(32)) x25_s9 (.D(write_data), .en(demultiplexer_5_out0[1]), .clk(clk), .Q(x25_s9_q), .clr(Reset));
  Register #(.width(32)) x2_sp (.D(write_data), .en(demultiplexer_2_out0[2]), .clk(clk), .Q(x2_sp_q), .clr(Reset));
  Register #(.width(32)) x10_a0 (.D(write_data), .en(demultiplexer_3_out0[2]), .clk(clk), .Q(x10_a0_q), .clr(Reset));
  Register #(.width(32)) x18_s2 (.D(write_data), .en(demultiplexer_4_out0[2]), .clk(clk), .Q(x18_s2_q), .clr(Reset));
  Register #(.width(32)) x26_s10 (.D(write_data), .en(demultiplexer_5_out0[2]), .clk(clk), .Q(x26_s10_q), .clr(Reset));
  Register #(.width(32)) x3_gp (.D(write_data), .en(demultiplexer_2_out0[3]), .clk(clk), .Q(x3_gp_q), .clr(Reset));
  Register #(.width(32)) x11_a1 (.D(write_data), .en(demultiplexer_3_out0[3]), .clk(clk), .Q(x11_a1_q), .clr(Reset));
  Register #(.width(32)) x19_s3 (.D(write_data), .en(demultiplexer_4_out0[3]), .clk(clk), .Q(x19_s3_q), .clr(Reset));
  Register #(.width(32)) x27_s11 (.D(write_data), .en(demultiplexer_5_out0[3]), .clk(clk), .Q(x27_s11_q), .clr(Reset));
  Register #(.width(32)) x4_tp (.D(write_data), .en(demultiplexer_2_out0[4]), .clk(clk), .Q(x4_tp_q), .clr(Reset));
  Register #(.width(32)) x12_a2 (.D(write_data), .en(demultiplexer_3_out0[4]), .clk(clk), .Q(x12_a2_q), .clr(Reset));
  Register #(.width(32)) x20_s4 (.D(write_data), .en(demultiplexer_4_out0[4]), .clk(clk), .Q(x20_s4_q), .clr(Reset));
  Register #(.width(32)) x28_t3 (.D(write_data), .en(demultiplexer_5_out0[4]), .clk(clk), .Q(x28_t3_q), .clr(Reset));
  Register #(.width(32)) x5_t0 (.D(write_data), .en(demultiplexer_2_out0[5]), .clk(clk), .Q(x5_t0_q), .clr(Reset));
  Register #(.width(32)) x13_a3 (.D(write_data), .en(demultiplexer_3_out0[5]), .clk(clk), .Q(x13_a3_q), .clr(Reset));
  Register #(.width(32)) x21_s5 (.D(write_data), .en(demultiplexer_4_out0[5]), .clk(clk), .Q(x21_s5_q), .clr(Reset));
  Register #(.width(32)) x29_t4 (.D(write_data), .en(demultiplexer_5_out0[5]), .clk(clk), .Q(x29_t4_q), .clr(Reset));
  Register #(.width(32)) x6_t1 (.D(write_data), .en(demultiplexer_2_out0[6]), .clk(clk), .Q(x6_t1_q), .clr(Reset));
  Register #(.width(32)) x14_a4 (.D(write_data), .en(demultiplexer_3_out0[6]), .clk(clk), .Q(x14_a4_q), .clr(Reset));
  Register #(.width(32)) x22_s6 (.D(write_data), .en(demultiplexer_4_out0[6]), .clk(clk), .Q(x22_s6_q), .clr(Reset));
  Register #(.width(32)) x30_t5 (.D(write_data), .en(demultiplexer_5_out0[6]), .clk(clk), .Q(x30_t5_q), .clr(Reset));
  Register #(.width(32)) x7_t2 (.D(write_data), .en(demultiplexer_2_out0[7]), .clk(clk), .Q(x7_t2_q), .clr(Reset));
  Register #(.width(32)) x15_a5 (.D(write_data), .en(demultiplexer_3_out0[7]), .clk(clk), .Q(x15_a5_q), .clr(Reset));
  Register #(.width(32)) x23_s7 (.D(write_data), .en(demultiplexer_4_out0[7]), .clk(clk), .Q(x23_s7_q), .clr(Reset));
  Register #(.width(32)) x31_t6 (.D(write_data), .en(demultiplexer_5_out0[7]), .clk(clk), .Q(x31_t6_q), .clr(Reset));
  Multiplexer #(.select(5), .width(32)) multiplexer_2 (
    .in0({32{1'b0}}), .in1(x1_ra_q), .in2(x2_sp_q), .in3(x3_gp_q), .in4(x4_tp_q), .in5(x5_t0_q),
    .in6(x6_t1_q), .in7(x7_t2_q), .in8(x8_s0_q), .in9(x9_s1_q), .in10(x10_a0_q), .in11(x11_a1_q),
    .in12(x12_a2_q), .in13(x13_a3_q), .in14(x14_a4_q), .in15(x15_a5_q), .in16(x16_a6_q), .in17(x17_a7_q),
    .in18(x18_s2_q), .in19(x19_s3_q), .in20(x20_s4_q), .in21(x21_s5_q), .in22(x22_s6_q), .in23(x23_s7_q),
    .in24(x24_s8_q), .in25(x25_s9_q), .in26(x26_s10_q), .in27(x27_s11_q), .in28(x28_t3_q), .in29(x29_t4_q),
    .in30(x30_t5_q), .in31(x31_t6_q), .out(rs1_data), .sel(rs1_index));
  Multiplexer #(.select(5), .width(32)) multiplexer_3 (
    .in0({32{1'b0}}), .in1(x1_ra_q), .in2(x2_sp_q), .in3(x3_gp_q), .in4(x4_tp_q), .in5(x5_t0_q),
    .in6(x6_t1_q), .in7(x7_t2_q), .in8(x8_s0_q), .in9(x9_s1_q), .in10(x10_a0_q), .in11(x11_a1_q),
    .in12(x12_a2_q), .in13(x13_a3_q), .in14(x14_a4_q), .in15(x15_a5_q), .in16(x16_a6_q), .in17(x17_a7_q),
    .in18(x18_s2_q), .in19(x19_s3_q), .in20(x20_s4_q), .in21(x21_s5_q), .in22(x22_s6_q), .in23(x23_s7_q),
    .in24(x24_s8_q), .in25(x25_s9_q), .in26(x26_s10_q), .in27(x27_s11_q), .in28(x28_t3_q), .in29(x29_t4_q),
    .in30(x30_t5_q), .in31(x31_t6_q), .out(rs2_data), .sel(rs2_index));

  // Other names for the same wires on the sheet: R = Reset; rd_index2_0[2:0] = rd_index[2:0];
  //   rd_index4_3[1:0] = rd_index[4:3]

  // Notes on the sheet:
  //   x0_zero
endmodule

module ALU (
  input  [31:0] rs1_val,
  input  [31:0] rs2_val,
  input  [31:0] PC_plus_4,
  input  AUIPC,
  input  [31:0] imm_out,
  input  ALUSrc,
  input  [3:0] ALUop,
  output [31:0] Result,
  output zero,
  output Lt,
  output Ltu
);

  wire [31:0] adder_1_out, and_1_out, bit_extender_1_out, bit_extender_2_out, or_1_out, rs1_val_t,
       rs2_or_imm, shifter_1_out, shifter_2_out, shifter_3_out, subtractor_1_out, subtractor_2_out, xor_1_out;

  Subtractor #(.width(32)) subtractor_1 (.a(PC_plus_4), .b(32'h4), .out(subtractor_1_out));  // open: bin, bout
  Multiplexer #(.width(32)) multiplexer_1 (.in0(rs1_val), .in1(subtractor_1_out), .out(rs1_val_t), .sel(AUIPC));
  Multiplexer #(.width(32)) multiplexer_2 (.in0(rs2_val), .in1(imm_out), .out(rs2_or_imm), .sel(ALUSrc));
  Comparator #(.width(32)) comparator_1 (.a(rs1_val_t), .b(rs2_or_imm), .lt(Lt));  // open: gt, eq
  Comparator #(.mode("unsigned"), .width(32)) comparator_2 (.a(rs1_val_t), .b(rs2_or_imm), .lt(Ltu));  // open: gt, eq
  Adder #(.width(32)) adder_1 (.a(rs1_val_t), .b(rs2_or_imm), .out(adder_1_out));  // open: cin, cout
  Subtractor #(.width(32)) subtractor_2 (.a(rs1_val_t), .b(rs2_or_imm), .out(subtractor_2_out));  // open: bin, bout
  Shifter #(.width(32)) shifter_1 (.in(rs1_val_t), .\dist (rs2_or_imm[4:0]), .out(shifter_1_out));
  assign bit_extender_1_out = {{31{1'b0}}, Lt};  // Bit_Extender bit_extender_1
  assign bit_extender_2_out = {{31{1'b0}}, Ltu};  // Bit_Extender bit_extender_2
  assign xor_1_out = rs1_val_t ^ rs2_or_imm;  // XOR_Gate xor_1, 32 bits wide
  Shifter #(.shift("lr"), .width(32)) shifter_2 (.in(rs1_val_t), .\dist (rs2_or_imm[4:0]), .out(shifter_2_out));
  Shifter #(.shift("ar"), .width(32)) shifter_3 (.in(rs1_val_t), .\dist (rs2_or_imm[4:0]), .out(shifter_3_out));
  assign or_1_out = rs1_val_t | rs2_or_imm;  // OR_Gate or_1, 32 bits wide
  assign and_1_out = rs1_val_t & rs2_or_imm;  // AND_Gate and_1, 32 bits wide
  Multiplexer #(.select(4), .width(32)) multiplexer_3 (
    .in0(adder_1_out), .in1(subtractor_2_out), .in2(shifter_1_out), .in3(bit_extender_1_out),
    .in4(bit_extender_2_out), .in5(xor_1_out), .in6(shifter_2_out), .in7(shifter_3_out), .in8(or_1_out),
    .in9(and_1_out), .in10(rs2_or_imm), .in11(rs1_val_t), .out(Result), .sel(ALUop));  // open: in12, in13, in14, in15
  Comparator #(.width(32)) comparator_3 (.a(Result), .b({32{1'b0}}), .eq(zero));  // open: gt, lt

  // Other names for the same wires on the sheet: shamt[4:0] = rs2_or_imm[4:0]

  // Notes on the sheet:
  //   SLT-0011
  //   SLTU-0100
  //   XOR-0101
  //   SRL-0110
  //   SRA-0111
  //   OR-1000
  //   AND-1001
  //   COPY-B-1010
  //   PASS-A-1011
  //   ADD-0000
  //   SUB-0001
  //   SLL-0010
endmodule

module CU (
  input  [31:0] instruction,
  output [12:0] control_word,
  output [3:0] ALUop
);

  // Probe on instruction[6:0]
  // Probe on instruction[14:12]
  // Probe on instruction[30]
  // Probe on instruction[6:0]
  ROM #(.addrWidth(11), .dataWidth(17)) rom_1 (
    .addr({instruction[30], instruction[14:12], instruction[6:0]}), .data({control_word, ALUop}));
  // Probe on {instruction[30], instruction[14:12], instruction[6:0]}

  // Other names for the same wires on the sheet: opcode[6:0] = instruction[6:0]; funct3[2:0] = instruction[14:12];
  //   funct7_bit = instruction[30]

  // Notes on the sheet:
  //   contents of rom_1 (hex, n*v repeats v):
  //   0 0 0 cc00 15*0 8400 0 0 0 18431 11*0 2410 15*0 8000 0 0 0 8430 43*0 231 0 0 0 9481 7*0 9140 19*0
  //   cc00 15*0 8402 0 0 0 18432 11*0 2410 15*0 8002 0 0 0 8430 43*0 231 0 0 0 9482 7*0 9142 19*0 cc00
  //   15*0 8403 0 0 0 18433 11*0 2410 15*0 8003 0 0 0 8430 43*0 2233 0 0 0 9483 7*0 9140 19*0 cc00 15*0
  //   8403 0 0 0 18434 11*0 2410 15*0 8003 0 0 0 8430 43*0 2234 0 0 0 9484 7*0 9144 19*0 cc00 15*0 8400 0
  //   0 0 18435 11*0 2410 15*0 8005 0 0 0 8430 43*0 233 0 0 0 9485 7*0 9145 19*0 cc00 15*0 8406 0 0 0
  //   18436 11*0 2410 15*0 8006 0 0 0 8430 43*0 231 0 0 0 9486 7*0 9146 19*0 cc01 15*0 8400 0 0 0 18438
  //   11*0 2411 15*0 8008 0 0 0 8431 43*0 2238 0 0 0 9488 7*0 9148 19*0 cc01 15*0 8409 0 0 0 18439 11*0
  //   2411 15*0 8009 0 0 0 8431 43*0 231 0 0 0 9489 7*0 9149 19*0 cc01 15*0 8400 0 0 0 18431 11*0 2411
  //   15*0 8001 0 0 0 8431 43*0 2231 0 0 0 9481 7*0 9141 19*0 cc01 15*0 8400 0 0 0 18432 11*0 2411 15*0
  //   8000 0 0 0 8431 43*0 231 0 0 0 9482 7*0 9142 19*0 cc01 15*0 8400 0 0 0 18433 11*0 2411 15*0 8000 0 0
  //   0 8431 43*0 2233 0 0 0 9483 7*0 9143 19*0 cc01 15*0 8400 0 0 0 18434 11*0 2411 15*0 8000 0 0 0 8431
  //   43*0 2234 0 0 0 9484 7*0 9144 19*0 cc01 15*0 8400 0 0 0 18435 11*0 2411 15*0 8000 0 0 0 8431 43*0
  //   231 0 0 0 9485 7*0 9145 19*0 cc01 15*0 8407 0 0 0 18437 11*0 2411 15*0 8007 0 0 0 8431 43*0 237 0 0
  //   0 9487 7*0 9147 19*0 cc01 15*0 8400 0 0 0 18438 11*0 2411 15*0 8000 0 0 0 8431 43*0 2238 0 0 0 9488
  //   7*0 9148 19*0 cc01 15*0 8400 0 0 0 18439 11*0 2411 15*0 8000 0 0 0 8431 43*0 231 0 0 0 9489 7*0 9149
endmodule

module DataMem (
  input  [31:0] addr_in,
  input  Reset,
  input  clk,
  input  [31:0] raw,
  input  MemWrite,
  input  [2:0] funct3,
  input  [31:0] write_data,
  output R,
  output ck,
  output [15:0] addr,
  output [31:0] raw_read_data,
  output mw,
  output [31:0] read_data,
  output [3:0] lm,
  output [31:0] write_data_out
);

  wire [3:0] sb_mask, sh_mask;
  wire [4:0] bit_extender_1_out, shift_amt;
  wire [31:0] LB, LBU, LH, LHU, mid_result, shifter_3_out, shifter_4_out, shifter_5_out;

  Multiplexer #(.select(2), .width(4)) multiplexer_1 (
    .in0(4'b0001), .in1(4'b0010), .in2(4'b0100), .in3(4'b1000), .out(sb_mask), .sel(addr_in[1:0]));
  Multiplexer #(.select(2), .width(4)) multiplexer_2 (
    .in0(4'b0011), .in2(4'b1100), .out(sh_mask), .sel(addr_in[1:0]));  // open: in1, in3
  Multiplexer #(.select(3), .width(4)) multiplexer_3 (
    .in0(sb_mask), .in1(sh_mask), .in2(4'b1111), .out(lm), .sel(funct3));  // open: in3, in4, in5, in6, in7
  Shifter #(.width(32)) shifter_1 (.in(write_data), .\dist (shift_amt), .out(mid_result));
  Multiplexer #(.select(3), .width(32)) multiplexer_4 (
    .in0(mid_result), .in1(mid_result), .in2(write_data), .out(write_data_out), .sel(funct3));  // open: in3, in4, in5, in6, in7
  assign bit_extender_1_out = {{3{1'b0}}, addr_in[1:0]};  // Bit_Extender bit_extender_1
  Shifter #(.width(5)) shifter_2 (.in(bit_extender_1_out), .\dist (3'b011), .out(shift_amt));
  Shifter #(.shift("lr"), .width(32)) shifter_3 (.in(raw), .\dist (shift_amt), .out(shifter_3_out));
  Shifter #(.width(32)) shifter_4 (.in(LBU), .\dist (5'b11000), .out(shifter_4_out));
  Shifter #(.width(32)) shifter_5 (.in(LHU), .\dist (5'b10000), .out(shifter_5_out));
  assign LBU = 32'hff & shifter_3_out;  // AND_Gate and_1, 32 bits wide
  assign LHU = 32'hffff & shifter_3_out;  // AND_Gate and_2, 32 bits wide
  Shifter #(.shift("ar"), .width(32)) shifter_6 (.in(shifter_4_out), .\dist (5'b11000), .out(LB));
  Shifter #(.shift("ar"), .width(32)) shifter_7 (.in(shifter_5_out), .\dist (5'b10000), .out(LH));
  Multiplexer #(.select(3), .width(32)) multiplexer_5 (
    .in0(LB), .in1(LH), .in2(raw), .in3({32{1'b0}}), .in4(LBU), .in5(LHU), .in6({32{1'b0}}),
    .in7({32{1'b0}}), .out(read_data), .sel(funct3));

  assign addr = {addr_in[15:2], 2'b00};
  assign ck = clk;
  assign mw = MemWrite;
  assign R = Reset;
  assign raw_read_data = raw;

  // Other names for the same wires on the sheet: offset[1:0] = addr_in[1:0]; f3[2:0] = funct3; LW[31:0] = raw
endmodule

module parser (
);

  wire AUIPC, button_1_out, clk, comparator_1_eq, funct7_bit;
  wire [2:0] funct3;
  wire [3:0] ALUop;
  wire [5:4] word_data;
  wire [6:0] opcode;
  wire [11:0] controlword;
  wire [16:0] multiplexer_1_out, ram_1_dout;

  Button button_1 (.out(button_1_out));
  Clock clock_1 (.out(clk));
  Counter #(.max('h7ff), .ongoal("stay"), .width(11)) counter_1 (
    .clr(button_1_out), .up(1'b1), .count(1'b1), .clk(clk), .Q({funct7_bit, funct3, opcode}));  // open: load, D, carry
  Comparator #(.width(12)) comparator_1 (.a(controlword), .b({12{1'b0}}), .eq(comparator_1_eq));  // open: gt, lt
  Multiplexer #(.width(17)) multiplexer_1 (
    .in0({AUIPC, controlword, ALUop}), .in1({17{1'b0}}), .out(multiplexer_1_out), .sel(comparator_1_eq));
  Comparator #(.width(7)) comparator_2 (.a(opcode), .b(7'b0010111), .eq(AUIPC));  // open: gt, lt
  RAM #(.addrWidth(11), .asyncread("true"), .dataWidth(17)) ram_1 (
    .addr({funct7_bit, funct3, opcode}), .we(1'b1), .oe(1'b1), .clk(clk), .din(multiplexer_1_out),
    .dout(ram_1_dout));
  ROM #(.addrWidth(7), .dataWidth(14)) word (.addr(opcode), .data({controlword, word_data}));
  // Probe on ram_1_dout
  // Probe on controlword
  ROM #(.addrWidth(6), .dataWidth(4)) ALUControl (.addr({word_data, funct7_bit, funct3}), .data(ALUop));

  // Notes on the sheet:
  //   contents of word (hex, n*v repeats v):
  //   0 0 0 3302 15*0 2103 0 0 0 210c 11*0 906 15*0 2003 0 0 0 210e 43*0 88c 0 0 0 2520 7*0 2451
  //   contents of ALUControl (hex, n*v repeats v):
  //   1 2 3 4 5 6 8 9 1 2 3 4 5 7 8 9 0 2 0 4 5 6 8 9 1 2 3 4 5 7 8 9 6*0 10*1 0 2 3 3 0 6 0 9 5*0 7
endmodule

module test (
);

  // RGB_Video rgb_video_1: pin names not known
endmodule

module cpu (
  input  reset,
  input  [31:0] data_in,
  input  clk,
  output [31:0] value,
  output [31:0] adress
);

  wire ALUSrc, AUIPC, Branch, branch_taken, comparator_1_eq, Lt, multiplexer_1_out, not_1_out, not_2_out,
       ram_1_p2, ram_1_p7, zero;
  wire [2:0] funct3;
  wire [3:0] ALUop, ram_1_p3;
  wire [7:0] datamem_1_write_data_out, datamem_1_write_data_out_2, datamem_1_write_data_out_3,
       datamem_1_write_data_out_4, undriven, undriven_2, undriven_3, undriven_4;
  wire [11:0] control_word;
  wire [15:0] ram_1_p1;
  wire [31:0] datamem_1_read_data, imm_b, imm_i, imm_j, imm_out, instruction, pc_1_pc_out, PC_plus_4,
       ram_read_data, rs1_val;

  PC pc_1 (
    .branch_taken(branch_taken), .jump(control_word[4]), .jalr(control_word[3]), .imm_b(imm_b),
    .imm_j(imm_j), .clk(clk), .reset(reset), .rs1_val(rs1_val), .imm_i(imm_i), .pc_out(pc_1_pc_out),
    .pc_plus_4(PC_plus_4));
  CU cu_1 (
    .instruction({instruction[31:15], funct3, instruction[11:0]}),
    .control_word({AUIPC, control_word[11:7], ALUSrc, Branch, control_word[4:0]}), .ALUop(ALUop));
  ROM #(.addrWidth(16), .dataWidth(32)) InstMem (
    .addr(pc_1_pc_out[17:2]), .data({instruction[31:15], funct3, instruction[11:0]}));
  // Probe on funct3
  not not_1 (not_1_out, zero);
  not not_2 (not_2_out, Lt);
  // Probe on ram_1_p1
  // Probe on {datamem_1_write_data_out_4, datamem_1_write_data_out_3, datamem_1_write_data_out_2, datamem_1_write_data_out}
  // RAM #(.addrWidth(16), .clearpin("true"), .enables("line"), .line("quad")) ram_1: pin names not known; wires that end beside it: ram_1_p1, ram_1_p2, ram_1_p3[0], ram_1_p3[1], ram_1_p3[2], ram_1_p3[3], ram_1_p7
  Multiplexer #(.select(3)) multiplexer_1 (
    .in0(zero), .in1(not_1_out), .in2(1'b0), .in3(1'b0), .in4(Lt), .in5(not_2_out), .in6(1'b0), .in7(1'b0),
    .out(multiplexer_1_out), .sel(funct3));
  and and_1 (branch_taken, multiplexer_1_out, Branch);
  DataMem datamem_1 (
    .R({reset, 1'bz}), .raw({undriven_4, undriven_3, undriven_2, undriven}), .clk({clk, ram_1_p7}),
    .funct3(funct3), .write_data(value), .MemWrite({control_word[9], ram_1_p2}), .addr_in(adress),
    .write_data_out({datamem_1_write_data_out_4, datamem_1_write_data_out_3, datamem_1_write_data_out_2, datamem_1_write_data_out}),
    .read_data(datamem_1_read_data), .lm(ram_1_p3), .addr(ram_1_p1));  // open: raw_read_data
  // Probe on adress
  // Probe on ram_read_data
  Multiplexer #(.width(32)) multiplexer_2 (
    .in0(datamem_1_read_data), .in1(data_in), .out(ram_read_data), .sel(comparator_1_eq));
  Comparator #(.width(32)) comparator_1 (.a(adress), .b(32'h214), .eq(comparator_1_eq));  // open: gt, lt
  // Probe on imm_out
  ImmGen immgen_1 (
    .imm_sel(control_word[2:0]), .instr({instruction[31:15], funct3, instruction[11:0]}), .type_b(imm_b),
    .type_i(imm_i), .type_j(imm_j), .imm_out(imm_out));
  // Probe on {AUIPC, control_word[11:7], ALUSrc, Branch, control_word[4:0]}
  // Probe on instruction[11:7]
  // Probe on control_word[8:7]
  RegFile regfile_1 (
    .rs2_index(instruction[24:20]), .rs1_index(instruction[19:15]), .ram_read_data(ram_read_data),
    .Pc_plus_4(PC_plus_4), .RegWrite(control_word[11]), .Reset(reset), .alu_result(adress),
    .rd_index(instruction[11:7]), .clk(clk), .MemtoReg(control_word[8:7]), .rs2_data(value),
    .rs1_data(rs1_val));
  ALU alu_1 (
    .ALUop(ALUop), .PC_plus_4(PC_plus_4), .rs1_val(rs1_val), .AUIPC(AUIPC), .ALUSrc(ALUSrc),
    .imm_out(imm_out), .rs2_val(value), .Result(adress), .zero(zero), .Lt(Lt));  // open: Ltu

  // Other names for the same wires on the sheet: alu_result[31:0] = adress; immSel[2:0] = control_word[2:0];
  //   jalr = control_word[3]; jal = control_word[4]; control_word (some bits) = {AUIPC, ALUSrc, Branch};
  //   MemToReg[1:0] = control_word[8:7]; MemWrite = control_word[9]; MemRead = control_word[10];
  //   RegWrite = control_word[11]; rd_index[4:0] = instruction[11:7]; instruction[14:12] = funct3;
  //   rs1_index[4:0] = instruction[19:15]; rs2_index[4:0] = instruction[24:20]; rs2_val[31:0] = value

  // Notes on the sheet:
  //   contents of InstMem (hex, n*v repeats v):
  //   10137 10113 2b7 3f428293 337 5f430313 628863 2a023 428293 ff5ff06f ac000ef 6f 7b7 3f07a503 d51713
  //   e54533 3ea7a823 1155713 e54533 3ea7a823 a5a5a737 5a570713 e50533 3ea7a823 551713 e54533 3ea7a823
  //   f57513 8067 20c02023 f57513 20a00223 f5f593 20b00423 21000793 78023 100713 e78023 78023 8067
  //   ff010113 12623 100006f c12783 178793 f12623 c12703 3200793 e797b3 c12703 fef762e3 1010113 8067
  //   fe010113 112e23 812c23 912a23 1212823 1312623 1412423 1512223 1612023 20000823 20c00793 100713
  //   e78023 78023 97 f24080e7 50493 97 f18080e7 50993 7b7 3f478793 700713 e78023 10e78023 600693 d780a3
  //   10e780a3 500693 d78123 10e78123 400693 d781a3 10e781a3 413 300006f 7b7 3f478793 8787b3 229637
  //   b2260613 1007c583 7c503 97 ef4080e7 140413 ff47413 100793 fc87f8e3 200913 b13 300413 13c0006f 100713
  //   14e40a63 78b13 413 79463 78b13 fff90713 7b7 3f478793 e787b3 7ca03 1007ca83 ff97713 fff70713 ff77713
  //   6c0006f 12040463 78b13 100413 fc5ff06f 300713 12e40263 78b13 200413 fb1ff06f 200713 e40863 78b13
  //   300413 f9dff06f 78b13 f95ff06f fff70693 7b7 3f478793 d78633 64583 e787b3 b78023 10064703 10e78023
  //   ff6f713 fc071ce3 e041663 7b7 3f478793 1007c783 c078a63 fff78793 ff7f793 737 3f470713 10f70023 7b7
  //   3f47c783 979a63 7b7 3f478793 1007c783 13378e63 613 a8593 a0513 97 dd0080e7 7b7 3f478793 229637
  //   b2260613 1007c583 7c503 97 db0080e7 ff0637 98593 48513 97 d9c080e7 21404783 7f7f793 ecfb08e3
  //   ec0786e3 5700713 eae78ae3 7700713 eae786e3 5300713 eee782e3 7300713 ece78ee3 4100713 eee782e3
  //   6100713 ece78ee3 4400713 eee784e3 6400713 eee780e3 78b13 e85ff06f f00793 f35ff06f 100793 2f40c63
  //   200793 4f40e63 300793 f2f414e3 7b7 3f47c783 f00693 d78663 178793 ff7f713 7b7 3ee78a23 f05ff06f 7b7
  //   3f478793 1007c783 f00693 d78663 178793 ff7f713 7b7 3f478793 10e78023 ed9ff06f 7b7 3f47c783 78c63
  //   fff78793 ff7f793 737 3ef70a23 eb9ff06f f00793 ff1ff06f 97 c60080e7 50493 97 c54080e7 50993 190913
  //   eadff06f 1234abcd
  //   Control Word
  //   bit 11 (RegWrite)
  //   bit 10 (MemRead)
  //   bit 9 (MemWrite)
  //   bits 8..7 (MemToReg[1:0])
  //   bit 6 (ALUSrc)
  //   bit 5 (Branch)
  //   bit 4 (Jump(JAL))
  //   bit 3 (Jalr)
  //   bits 2..0 (ImmSel[2:0])
endmodule
